// Logisim project PC_insturctions.circ as structural Verilog: 3 circuits, main circuit main
module main (
  input  branch,
  input  [15:0] branch_address
);

  wire CLK, not_1_out;
  wire [3:0] a, b, d, opcode;
  wire [15:0] PC_q;

  not not_1 (not_1_out, branch);
  Clock u_CLK (.out(CLK));
  Counter #(.max('hffff), .width(16)) PC (
    .load(branch), .count(not_1_out), .clk(CLK), .D(branch_address), .Q(PC_q));  // open: clr, up, carry
  ROM #(.addrWidth(16), .dataWidth(16)) rom_1 (.addr(PC_q), .data({opcode, d, a, b}));

  // Other names for the same wires on the sheet: B_Add[15:0] = branch_address

  // Notes on the sheet:
  //   contents of rom_1 (hex, n*v repeats v):
  //   3160 e101 f1ff e216 f200 a312 d423 35c6 3645 e901 f9c0 6609 4709 3815
endmodule

module theRAM (
  input  [15:0] Rd_out,
  input  [15:0] Rb,
  input  b12,
  input  [3:0] a,
  input  [3:0] opcode,
  output [15:0] RAM_out
);

  wire CLK, LD, ST;
  wire [15:0] adder_1_out, bit_extender_1_out;

  Clock u_CLK (.out(CLK));
  and and_1 (LD, ~opcode[1], opcode[2], ~opcode[3]);  // AND_Gate
  and and_2 (ST, opcode[1], opcode[2], ~opcode[3]);  // AND_Gate
  Adder #(.width(16)) adder_1 (.a(Rb), .b(bit_extender_1_out), .out(adder_1_out));  // open: cin, cout
  assign bit_extender_1_out = {{11{1'b0}}, {b12, a}};  // Bit_Extender bit_extender_1
  RAM #(.addrWidth(16), .asyncread("true"), .dataWidth(16)) theRAM (
    .addr(adder_1_out), .we(ST), .oe(LD), .clk(CLK), .din(Rd_out), .dout(RAM_out));

  // Notes on the sheet:
  //   opcode controls load/store
endmodule

module flagBank (
  input  [4:0] flagsIn,
  input  Clock,
  output [4:0] flagsOut
);

  D_Flip_Flop sign (.clk(Clock), .D(flagsIn[0]), .Q(flagsOut[0]));  // open: Qn, preset, reset
  D_Flip_Flop zero (.clk(Clock), .D(flagsIn[1]), .Q(flagsOut[1]));  // open: Qn, preset, reset
  D_Flip_Flop overflow (.clk(Clock), .D(flagsIn[2]), .Q(flagsOut[2]));  // open: Qn, preset, reset
  D_Flip_Flop carry (.clk(Clock), .D(flagsIn[3]), .Q(flagsOut[3]));  // open: Qn, preset, reset
  D_Flip_Flop carry_block (.clk(Clock), .D(flagsIn[4]), .Q(flagsOut[4]));  // open: Qn, preset, reset
endmodule
