// Logisim project Lab2H_Template.circ as structural Verilog: 28 circuits, main circuit main
module main (
  input  BrkEnable,
  input  reset
);

  wire clk, clock_1_out, cpu_1_load, store;
  wire [4:0] cpu_1_flags;
  wire [15:0] Break_q, DataRAM_dout, FP, PC, ProgramROM_data, R1, R2, R3, R4, R5, R6, R7, R8, R9, R10, R11,
       R12, R13, RAM_addr, RAM_data, SP;

  Register #(.width(16)) Break (.D({16{1'b0}}), .en(1'b0), .clk(1'b0), .Q(Break_q), .clr(1'b0));
  ROM #(.addrWidth(16), .dataWidth(16)) ProgramROM (.addr(PC), .data(ProgramROM_data));
  RAM #(.addrWidth(16), .dataWidth(16), .enables("line")) DataRAM (
    .addr(RAM_addr), .we(store), .clk(clk), .din(RAM_data), .dout(DataRAM_dout));
  Hex_Digit_Display #(.decimalPoint("false")) hex_digit_display_1 (.value(PC[15:12]));
  Hex_Digit_Display #(.decimalPoint("false")) hex_digit_display_2 (.value(PC[11:8]));
  Hex_Digit_Display #(.decimalPoint("false")) hex_digit_display_3 (.value(PC[7:4]));
  Hex_Digit_Display #(.decimalPoint("false")) hex_digit_display_4 (.value(PC[3:0]));
  Clock clock_1 (.out(clock_1_out));
  Hex_Digit_Display #(.decimalPoint("false")) op (.value(ProgramROM_data[15:12]));
  Breakpoint breakpoint_1 (.PC(PC), .Target(Break_q), .Enable(BrkEnable), .Clk(clock_1_out), .ClkOut(clk));
  Hex_Digit_Display #(.decimalPoint("false")) d (.value(ProgramROM_data[11:8]));
  Hex_Digit_Display #(.decimalPoint("false")) a (.value(ProgramROM_data[7:4]));
  Hex_Digit_Display #(.decimalPoint("false")) hex_digit_display_5 (.value(R1[15:12]));
  Hex_Digit_Display #(.decimalPoint("false")) hex_digit_display_6 (.value(R1[11:8]));
  Hex_Digit_Display #(.decimalPoint("false")) hex_digit_display_7 (.value(R6[15:12]));
  Hex_Digit_Display #(.decimalPoint("false")) hex_digit_display_8 (.value(R6[11:8]));
  Hex_Digit_Display #(.decimalPoint("false")) hex_digit_display_9 (.value(R11[15:12]));
  Hex_Digit_Display #(.decimalPoint("false")) hex_digit_display_10 (.value(R11[11:8]));
  Hex_Digit_Display #(.decimalPoint("false")) b (.value(ProgramROM_data[3:0]));
  Hex_Digit_Display #(.decimalPoint("false")) hex_digit_display_11 (.value(R1[7:4]));
  Hex_Digit_Display #(.decimalPoint("false")) hex_digit_display_12 (.value(R1[3:0]));
  Hex_Digit_Display #(.decimalPoint("false")) hex_digit_display_13 (.value(R6[7:4]));
  Hex_Digit_Display #(.decimalPoint("false")) hex_digit_display_14 (.value(R6[3:0]));
  Hex_Digit_Display #(.decimalPoint("false")) hex_digit_display_15 (.value(R11[7:4]));
  Hex_Digit_Display #(.decimalPoint("false")) hex_digit_display_16 (.value(R11[3:0]));
  Hex_Digit_Display #(.decimalPoint("false")) hex_digit_display_17 (.value(R2[15:12]));
  Hex_Digit_Display #(.decimalPoint("false")) hex_digit_display_18 (.value(R7[15:12]));
  Hex_Digit_Display #(.decimalPoint("false")) hex_digit_display_19 (.value(R12[15:12]));
  CPU cpu_1 (
    .clk(clk), .reset(reset), .instruction(ProgramROM_data), .ram_in(DataRAM_dout), .PC_out(PC),
    .flags(cpu_1_flags), .ram_addr(RAM_addr), .ram_data(RAM_data), .Load(cpu_1_load), .Store(store),
    .rg1({R4, R3, R2, R1}), .rg2({R8, R7, R6, R5}), .rg3({R12, R11, R10, R9}), .rg4({SP, FP, R13}));
  // NoConnect on cpu_1_load
  Hex_Digit_Display #(.decimalPoint("false")) hex_digit_display_20 (.value(R2[11:8]));
  Hex_Digit_Display #(.decimalPoint("false")) hex_digit_display_21 (.value(R2[7:4]));
  Hex_Digit_Display #(.decimalPoint("false")) hex_digit_display_22 (.value(R7[11:8]));
  Hex_Digit_Display #(.decimalPoint("false")) hex_digit_display_23 (.value(R7[7:4]));
  Hex_Digit_Display #(.decimalPoint("false")) hex_digit_display_24 (.value(R12[11:8]));
  Hex_Digit_Display #(.decimalPoint("false")) hex_digit_display_25 (.value(R12[7:4]));
  LED Cb (.in(cpu_1_flags[4]));
  Hex_Digit_Display #(.decimalPoint("false")) hex_digit_display_26 (.value(R2[3:0]));
  Hex_Digit_Display #(.decimalPoint("false")) hex_digit_display_27 (.value(R3[15:12]));
  Hex_Digit_Display #(.decimalPoint("false")) hex_digit_display_28 (.value(R7[3:0]));
  Hex_Digit_Display #(.decimalPoint("false")) hex_digit_display_29 (.value(R8[15:12]));
  Hex_Digit_Display #(.decimalPoint("false")) hex_digit_display_30 (.value(R12[3:0]));
  Hex_Digit_Display #(.decimalPoint("false")) hex_digit_display_31 (.value(R13[15:12]));
  LED C (.in(cpu_1_flags[3]));
  LED V (.in(cpu_1_flags[2]));
  LED Z (.in(cpu_1_flags[1]));
  Hex_Digit_Display #(.decimalPoint("false")) hex_digit_display_32 (.value(R3[11:8]));
  Hex_Digit_Display #(.decimalPoint("false")) hex_digit_display_33 (.value(R3[7:4]));
  Hex_Digit_Display #(.decimalPoint("false")) hex_digit_display_34 (.value(R8[11:8]));
  Hex_Digit_Display #(.decimalPoint("false")) hex_digit_display_35 (.value(R8[7:4]));
  Hex_Digit_Display #(.decimalPoint("false")) hex_digit_display_36 (.value(R13[11:8]));
  Hex_Digit_Display #(.decimalPoint("false")) hex_digit_display_37 (.value(R13[7:4]));
  LED S (.in(cpu_1_flags[0]));
  Hex_Digit_Display #(.decimalPoint("false")) hex_digit_display_38 (.value(R3[3:0]));
  Hex_Digit_Display #(.decimalPoint("false")) hex_digit_display_39 (.value(R8[3:0]));
  Hex_Digit_Display #(.decimalPoint("false")) hex_digit_display_40 (.value(R13[3:0]));
  Hex_Digit_Display #(.decimalPoint("false")) hex_digit_display_41 (.value(R4[11:8]));
  Hex_Digit_Display #(.decimalPoint("false")) hex_digit_display_42 (.value(R4[15:12]));
  Hex_Digit_Display #(.decimalPoint("false")) hex_digit_display_43 (.value(R9[11:8]));
  Hex_Digit_Display #(.decimalPoint("false")) hex_digit_display_44 (.value(R9[15:12]));
  Hex_Digit_Display #(.decimalPoint("false")) hex_digit_display_45 (.value(FP[11:8]));
  Hex_Digit_Display #(.decimalPoint("false")) hex_digit_display_46 (.value(FP[15:12]));
  Hex_Digit_Display #(.decimalPoint("false")) hex_digit_display_47 (.value(R4[7:4]));
  Hex_Digit_Display #(.decimalPoint("false")) hex_digit_display_48 (.value(R4[3:0]));
  Hex_Digit_Display #(.decimalPoint("false")) hex_digit_display_49 (.value(R9[7:4]));
  Hex_Digit_Display #(.decimalPoint("false")) hex_digit_display_50 (.value(R9[3:0]));
  Hex_Digit_Display #(.decimalPoint("false")) hex_digit_display_51 (.value(FP[7:4]));
  Hex_Digit_Display #(.decimalPoint("false")) hex_digit_display_52 (.value(FP[3:0]));
  Hex_Digit_Display #(.decimalPoint("false")) hex_digit_display_53 (.value(R5[15:12]));
  Hex_Digit_Display #(.decimalPoint("false")) hex_digit_display_54 (.value(R5[11:8]));
  Hex_Digit_Display #(.decimalPoint("false")) hex_digit_display_55 (.value(R10[15:12]));
  Hex_Digit_Display #(.decimalPoint("false")) hex_digit_display_56 (.value(R10[11:8]));
  Hex_Digit_Display #(.decimalPoint("false")) hex_digit_display_57 (.value(SP[15:12]));
  Hex_Digit_Display #(.decimalPoint("false")) hex_digit_display_58 (.value(SP[11:8]));
  Hex_Digit_Display #(.decimalPoint("false")) hex_digit_display_59 (.value(R5[7:4]));
  Hex_Digit_Display #(.decimalPoint("false")) hex_digit_display_60 (.value(R5[3:0]));
  Hex_Digit_Display #(.decimalPoint("false")) hex_digit_display_61 (.value(R10[7:4]));
  Hex_Digit_Display #(.decimalPoint("false")) hex_digit_display_62 (.value(R10[3:0]));
  Hex_Digit_Display #(.decimalPoint("false")) hex_digit_display_63 (.value(SP[7:4]));
  Hex_Digit_Display #(.decimalPoint("false")) hex_digit_display_64 (.value(SP[3:0]));

  // Notes on the sheet:
  //   contents of ProgramROM (hex, n*v repeats v):
  //   3160 e208 e101 c112 32c0 9fe
  //   PC
  //   Instruction
  //   Flags
  //   Register Displays
endmodule

module add_sub (
  input  [4:0] f_in,
  input  [15:0] Ra,
  input  [15:0] Rb,
  input  [3:0] opcode,
  output [15:0] result,
  output [4:0] f_out
);

  wire multiplexer_2_out, xnor_1_out, xor_1_out;
  wire [15:0] multiplexer_1_out, not_1_out;

  Multiplexer #(.width(16)) multiplexer_1 (.in0(Rb), .in1(not_1_out), .out(multiplexer_1_out), .sel(opcode[0]));
  assign not_1_out = ~Rb;  // NOT_Gate not_1, 16 bits wide
  Multiplexer multiplexer_2 (.in0(f_in[3]), .in1(opcode[0]), .out(multiplexer_2_out), .sel(f_in[4]));
  Adder #(.width(16)) adder_1 (
    .a(Ra), .b(multiplexer_1_out), .out({f_out[0], result[14:0]}), .cin(multiplexer_2_out), .cout(f_out[3]));
  xnor xnor_1 (xnor_1_out, Ra[15], multiplexer_1_out[15]);
  xor xor_1 (xor_1_out, f_out[0], Ra[15]);
  and and_1 (f_out[2], xor_1_out, xnor_1_out);
  nor nor_1 (f_out[1], result[0], result[1], result[2], result[3], result[4], result[5], result[6], result[7], result[8], result[9], result[10], result[11], result[12], result[13], result[14], f_out[0]);

  assign f_out[4] = f_in[4];
  assign result[15] = f_out[0];
endmodule

module ALSU (
  input  [4:0] flags_in,
  input  [15:0] Ra,
  input  [15:0] Rb,
  input  [15:0] Rd,
  input  [15:0] instruction,
  output [15:0] result,
  output [4:0] f_out
);

  ALSU_body alsu_body_1 (
    .flags_in(flags_in), .Ra(Ra), .Rb(Rb), .Rd(Rd), .instruction(instruction), .result(result), .f_out(f_out));
endmodule

module ALSU_body (
  input  [4:0] flags_in,
  input  [15:0] Ra,
  input  [15:0] Rb,
  input  [15:0] Rd,
  input  [15:0] instruction,
  output [15:0] result,
  output [4:0] f_out
);

  wire [4:0] asf, Luf, mulf, shiftf;
  wire [15:0] add_sub_1_result, lu_1_result, mul_1_result, sethi_1_result, setlo_1_result, shifts_1_result;

  shifts shifts_1 (
    .flags_in(flags_in), .Rb(Rb), .Rd(Rd), .b0_3(instruction[3:0]), .b4_7(instruction[7:4]),
    .b8_11(instruction[11:8]), .result(shifts_1_result), .f_out(shiftf));
  LU lu_1 (.Ra(Ra), .Rb(Rb), .opCode(instruction[15:12]), .f_in(flags_in), .result(lu_1_result), .f_out(Luf));
  add_sub add_sub_1 (
    .f_in(flags_in), .Ra(Ra), .Rb(Rb), .opcode(instruction[15:12]), .result(add_sub_1_result), .f_out(asf));
  MUL mul_1 (.f_in(flags_in), .Ra(Ra), .Rb(Rb), .result(mul_1_result), .f_out(mulf));
  setlo setlo_1 (.b0_3(instruction[3:0]), .b4_7(instruction[7:4]), .result(setlo_1_result));
  sethi sethi_1 (.Rb(Rd), .b0_3(instruction[3:0]), .b4_7(instruction[7:4]), .result(sethi_1_result));
  Multiplexer #(.select(4), .width(16)) multiplexer_1 (
    .in0({16{1'b0}}), .in1({16{1'b0}}), .in2({16{1'b0}}), .in3(shifts_1_result), .in4({16{1'b0}}),
    .in5({16{1'b0}}), .in6({16{1'b0}}), .in7({16{1'b0}}), .in8(lu_1_result), .in9(lu_1_result),
    .in10(add_sub_1_result), .in11(add_sub_1_result), .in12(mul_1_result), .in13(lu_1_result),
    .in14(setlo_1_result), .in15(sethi_1_result), .out(result), .sel(instruction[15:12]));
  Multiplexer #(.select(4), .width(5)) multiplexer_2 (
    .in0(flags_in), .in1(flags_in), .in2(flags_in), .in3(shiftf), .in4(flags_in), .in5(flags_in),
    .in6(flags_in), .in7(flags_in), .in8(Luf), .in9(Luf), .in10(asf), .in11(asf), .in12(mulf), .in13(Luf),
    .in14(flags_in), .in15(flags_in), .out(f_out), .sel(instruction[15:12]));

  // Other names for the same wires on the sheet: f_in[4:0] = flags_in; b0_3[3:0] = instruction[3:0];
  //   b4_7[3:0] = instruction[7:4]; b8_11[3:0] = instruction[11:8]; opc[3:0] = instruction[15:12]

  // Notes on the sheet:
  //   NOTICE: everything that can be computed will be, while only the result expected given the opcode will be pushed to the result
  //   STORE does not modify flags, LOAD changes s and z
  //   (but for now just output same flags, will change in memory circuit)
endmodule

module ASL (
  input  [4:0] flags,
  input  [15:0] Rb,
  output [15:0] result,
  output [4:0] f_out
);

  and and_1 (result[0], ~flags[4], flags[3]);  // AND_Gate
  xor xor_1 (f_out[2], Rb[14], Rb[15]);
  Comparator #(.width(16)) comparator_1 (.a({Rb[14:0], result[0]}), .b({16{1'b0}}), .eq(f_out[1]));  // open: gt, lt

  assign {f_out[4:3], f_out[0]} = {flags[4], Rb[15:14]};
  assign result[15:1] = Rb[14:0];

  // Other names for the same wires on the sheet: s_out = Rb[14]; z_out = f_out[1]; v_out = f_out[2]; c_out = Rb[15]
endmodule

module ASR (
  input  [4:0] flags,
  input  [15:0] Rb,
  output [15:0] result,
  output [4:0] f_out
);

  Shifter #(.shift("ar"), .width(16)) shifter_1 (.in(Rb), .\dist (4'b0001), .out(result));
  Comparator #(.width(16)) comparator_1 (.a(result), .b({16{1'b0}}), .eq(f_out[1]), .lt(f_out[0]));  // open: gt

  assign f_out[4:2] = {flags[4], Rb[0], flags[2]};

  // Other names for the same wires on the sheet: bit_shift_out = Rb[0]

  // Notes on the sheet:
  //   the bit got shifted out is the new carry
  //   ASR igores incoming carry, always producing a result that's half of the signed value
endmodule

module Branching (
  input  [4:0] Flags,
  input  [3:0] d,
  output Branch
);

  wire multiplexer_1_out, or_1_out, or_2_out, xor_1_out;

  xor xor_1 (xor_1_out, Flags[0], Flags[2]);
  or or_1 (or_1_out, xor_1_out, Flags[1]);
  or or_2 (or_2_out, Flags[1], ~Flags[3]);  // OR_Gate
  Multiplexer #(.select(3)) multiplexer_1 (
    .in0(1'b1), .in1(xor_1_out), .in2(or_1_out), .in3(or_2_out), .in4(Flags[1]), .in5(Flags[3]),
    .in6(Flags[0]), .in7(Flags[2]), .out(multiplexer_1_out), .sel(d[3:1]));
  xor xor_2 (Branch, multiplexer_1_out, d[0]);

  // Notes on the sheet:
  //   carry block
  //   sign
  //   zero
  //   overflow
  //   carry
endmodule

module Breakpoint (
  input  [15:0] PC,
  input  [15:0] Target,
  input  Enable,
  input  Clk,
  output ClkOut
);

  wire comparator_1_eq, nand_1_out;

  Comparator #(.width(16)) comparator_1 (.a(PC), .b(Target), .eq(comparator_1_eq));  // open: gt, lt
  nand nand_1 (nand_1_out, comparator_1_eq, Enable);
  and and_1 (ClkOut, nand_1_out, Clk);
endmodule

module control_unit (
  input  [15:0] instruction,
  input  [4:0] flags,
  input  [15:0] PC,
  input  [15:0] Rb,
  output load,
  output store,
  output branch,
  output CaRt,
  output [15:0] jump_to
);

  wire and_1_out, branching_1_branch, xor_1_out;
  wire [15:0] adder_1_out, bit_extender_1_out;

  and and_1 (and_1_out, ~instruction[13], ~instruction[14], ~instruction[15]);  // AND_Gate
  and and_2 (CaRt, ~instruction[15], ~instruction[14], instruction[13], ~instruction[12], ~instruction[8], ~instruction[9]);  // AND_Gate
  assign bit_extender_1_out = {{8{instruction[7]}}, instruction[7:0]};  // Bit_Extender bit_extender_1
  Adder #(.width(16)) adder_1 (.a(PC), .b(bit_extender_1_out), .out(adder_1_out), .cin(1'b0));  // open: cout
  xor xor_1 (xor_1_out, CaRt, instruction[12]);
  Multiplexer #(.width(16)) multiplexer_1 (.in0(adder_1_out), .in1(Rb), .out(jump_to), .sel(xor_1_out));
  and and_3 (load, ~instruction[13], instruction[14], ~instruction[15]);  // AND_Gate
  and and_4 (store, instruction[13], instruction[14], ~instruction[15]);  // AND_Gate
  Branching branching_1 (.Flags(flags), .d(instruction[11:8]), .Branch(branching_1_branch));
  and and_5 (branch, branching_1_branch, and_1_out);

  // Notes on the sheet:
  //   register branching
  //   offset
  //    Check to see if we need to branch/jump
  //   If we are branching, where are we going?
  //   If register branching, jump to Rb
  //   Otherwise, relative branching: jump to PC + offest
  //   CALL: Call func at Rb, new stack frame at Ra
  //   R12 is the new value of the FP, R13 is the branch address
  //   RETURN: jump/return if return address in Rb & caller's FP in Ra
endmodule

module CPU (
  input  clk,
  input  reset,
  input  [15:0] instruction,
  input  [15:0] ram_in,
  output [15:0] PC_out,
  output [4:0] flags,
  output [15:0] ram_addr,
  output [15:0] ram_data,
  output Load,
  output Store,
  output [63:0] rg1,
  output [63:0] rg2,
  output [63:0] rg3,
  output [47:0] rg4
);

  wire control_unit_1_branch, control_unit_1_cart, ctr16_1_we, should_branch;
  wire [4:0] alsu_flags, mem_flags_1_f_out, multiplexer_2_out;
  wire [15:0] addr, alsu_out, ctr16_1_q, multiplexer_1_out, Rb, registerbank_1_ra_out, registerbank_1_rd_out;

  CTR16 ctr16_1 (.Load(should_branch), .D(addr), .Enable(1'b1), .Current(PC_out), .Q(ctr16_1_q), .WE(ctr16_1_we));
  Register #(.width(16)) PC (.D(ctr16_1_q), .en(ctr16_1_we), .clk(clk), .Q(PC_out), .clr(reset));
  mem_flags mem_flags_1 (.f_in(flags), .ram_in(ram_in), .f_out(mem_flags_1_f_out));
  Multiplexer #(.width(16)) multiplexer_1 (.in0(alsu_out), .in1(ram_in), .out(multiplexer_1_out), .sel(Load));
  control_unit control_unit_1 (
    .instruction(instruction), .flags(flags), .PC(PC_out), .Rb(Rb), .load(Load), .store(Store),
    .branch(control_unit_1_branch), .CaRt(control_unit_1_cart), .jump_to(addr));
  Multiplexer #(.width(5)) multiplexer_2 (
    .in0(alsu_flags), .in1(mem_flags_1_f_out), .out(multiplexer_2_out), .sel(Load));
  xor xor_1 (should_branch, control_unit_1_branch, control_unit_1_cart);
  FlagBank flagbank_1 (.reset(reset), .flagsIn(multiplexer_2_out), .clock(clk), .flagsOut(flags));
  RegisterBank registerbank_1 (
    .reset(reset), .Rd_in(multiplexer_1_out), .Clock(clk), .PC_in(PC_out), .Instruction(instruction),
    .STORE(Store), .Ra_out(registerbank_1_ra_out), .Rb_out(Rb), .Rd_out(registerbank_1_rd_out), .Rg_1(rg1),
    .Rg_2(rg2), .Rg_3(rg3), .Rg_4(rg4));
  ALSU alsu_1 (
    .flags_in(flags), .Ra(registerbank_1_ra_out), .Rb(Rb), .Rd(registerbank_1_rd_out),
    .instruction(instruction), .result(alsu_out), .f_out(alsu_flags));
  load_store load_store_1 (
    .Rb(Rb), .Rd(registerbank_1_rd_out), .instruction(instruction), .addr(ram_addr), .Q(ram_data));

  // Other names for the same wires on the sheet: current_flags[4:0] = flags

  // Notes on the sheet:
  //   relevant CPU inputs
  //   (1) Begin by using the PC to read the current
  //   instruction from memory (via ROM)
  //   If we are jumping to a different instruction (via branch, or call/return),
  //   find the location of that instruction. Also control load/store
  //   (2) We need to find the values of Rd, Ra, and Rb.
  //   So, we go through the register bank...
  //   (3) Now that we have the operation & registers,
  //   we can perform the operation.
  //   Either ALSU or Memory.
  //   (4) Update the flags after the operation.
endmodule

module CTR16 (
  input  [15:0] Current,
  input  Load,
  input  [15:0] D,
  input  Enable,
  output [15:0] Q,
  output WE
);

  wire [15:0] adder_1_out;

  Adder #(.width(16)) adder_1 (.a(Current), .b({16{1'b0}}), .out(adder_1_out), .cin(Enable));  // open: cout
  Multiplexer #(.width(16)) multiplexer_1 (.in0(adder_1_out), .in1(D), .out(Q), .sel(Load));

  assign WE = 1'b1;
endmodule

module FlagBank (
  input  reset,
  input  [4:0] flagsIn,
  input  clock,
  output [4:0] flagsOut
);

  Register #(.width(5)) Flags (.D(flagsIn), .en(1'b1), .clk(clock), .Q(flagsOut), .clr(reset));

  // Other names for the same wires on the sheet: Sign = flagsOut[0]; Zero = flagsOut[1]; Overflow = flagsOut[2];
  //   Carry = flagsOut[3]; CarryBlock = flagsOut[4]
endmodule

module flags (
  input  [4:0] flags_in,
  input  [15:0] Rd,
  input  [3:0] b0_3,
  input  [3:0] b4_7,
  input  [3:0] b8_11,
  output [15:0] result,
  output [4:0] flags_out
);

  wire and_2_out;
  wire [4:0] and_1_out, multiplexer_1_out, or_1_out;
  wire [15:0] bit_extender_1_out;

  assign or_1_out = flags_in | {b8_11[0], b0_3};  // OR_Gate or_1, 5 bits wide
  assign and_1_out = flags_in & ~{b8_11[0], b0_3};  // AND_Gate and_1, 5 bits wide
  Multiplexer #(.select(2), .width(5)) multiplexer_1 (
    .in0(or_1_out), .in1({b8_11[0], b0_3}), .in2(and_1_out), .in3({flags_in[4], b0_3}),
    .out(multiplexer_1_out), .sel(b8_11[3:2]));
  assign bit_extender_1_out = {{11{1'b0}}, multiplexer_1_out};  // Bit_Extender bit_extender_1
  Multiplexer #(.width(16)) multiplexer_2 (.in0(Rd), .in1(bit_extender_1_out), .out(result), .sel(and_2_out));
  and and_2 (and_2_out, ~b0_3[3], b4_7[0]);  // AND_Gate
  Multiplexer #(.select(2), .width(5)) multiplexer_3 (
    .in0(multiplexer_1_out), .in1(multiplexer_1_out), .in2(flags_in), .in3(Rd[4:0]), .out(flags_out),
    .sel({b4_7[0], b0_3[3]}));
endmodule

module INC_DEC (
  input  [4:0] flags_in,
  input  [15:0] Rd,
  input  [3:0] b0_3,
  input  [3:0] b4_7,
  output [15:0] result,
  output [4:0] flags_out
);

  wire xnor_1_out, xor_1_out;
  wire [15:0] adder_1_out, bit_extender_1_out, multiplexer_1_out, not_1_out;

  assign bit_extender_1_out = {{10{1'b0}}, {b4_7[1:0], b0_3}};  // Bit_Extender bit_extender_1
  Adder #(.width(16)) adder_1 (.a(bit_extender_1_out), .b({16{1'b0}}), .out(adder_1_out), .cin(1'b1));  // open: cout
  Multiplexer #(.width(16)) multiplexer_1 (.in0(adder_1_out), .in1(not_1_out), .out(multiplexer_1_out), .sel(b4_7[2]));
  assign not_1_out = ~adder_1_out;  // NOT_Gate not_1, 16 bits wide
  Adder #(.width(16)) adder_2 (.a(Rd), .b(multiplexer_1_out), .out(result), .cin(b4_7[2]), .cout(flags_out[3]));
  xor xor_1 (xor_1_out, result[15], Rd[15]);
  xnor xnor_1 (xnor_1_out, Rd[15], multiplexer_1_out[15]);
  and and_1 (flags_out[2], xor_1_out, xnor_1_out);
  Comparator #(.width(16)) comparator_1 (.a(result), .b({16{1'b0}}), .eq(flags_out[1]), .lt(flags_out[0]));  // open: gt

  assign flags_out[4] = flags_in[4];

  // Notes on the sheet:
  //   b6 is inc/dec
  //   b0_5 as delta (unsigned, add 1 to get epsilon)
  //   inc/dec ignores incoming carry
endmodule

module load_store (
  input  [15:0] Rb,
  input  [15:0] Rd,
  input  [15:0] instruction,
  output [15:0] addr,
  output [15:0] Q
);

  wire [15:0] bit_extender_1_out;

  assign bit_extender_1_out = {{11{1'b0}}, {instruction[12], instruction[7:4]}};  // Bit_Extender bit_extender_1
  Adder #(.width(16)) adder_1 (.a(Rb), .b(bit_extender_1_out), .out(addr), .cin(1'b0));  // open: cout

  assign Q = Rd;
endmodule

module LSL (
  input  [4:0] flags,
  input  [15:0] Rb,
  output [15:0] result,
  output [4:0] f_out
);

  Shifter #(.width(16)) shifter_1 (.in(Rb), .\dist (4'b0001), .out(result));
  Comparator #(.width(16)) comparator_1 (.a(result), .b({16{1'b0}}), .eq(f_out[1]), .lt(f_out[0]));  // open: gt

  assign f_out[4:2] = {flags[4], Rb[15], flags[2]};

  // Notes on the sheet:
  //   this basically shifts all the digits left by one
  //   then, the value of C ^ F4' will be in the least significant bit 
  //   all comparator like this is to decide the sign and zero flags output
  //   c became the bit that's shifted out
endmodule

module LSL8 (
  input  [4:0] flags,
  input  [15:0] Rb,
  output [15:0] result,
  output [4:0] f_out
);

  Comparator #(.width(16)) comparator_1 (
    .a({Rb[7:0], {8{1'b0}}}), .b({16{1'b0}}), .eq(f_out[1]), .lt(f_out[0]));  // open: gt

  assign f_out[4:2] = flags[4:2];
  assign result = {Rb[7:0], {8{1'b0}}};

  // Notes on the sheet:
  //   LSL8 instruction
  //   the eight-bit shift operations shift in zeros, regardless of the carry-blog(F4) flag.
endmodule

module LSR (
  input  [4:0] flags,
  input  [15:0] Rb,
  output [15:0] result,
  output [4:0] f_out
);

  and and_1 (result[15], Rb[0], ~flags[4]);  // AND_Gate
  Comparator #(.width(16)) comparator_1 (
    .a({result[15], Rb[15:1]}), .b({16{1'b0}}), .eq(f_out[1]), .lt(f_out[0]));  // open: gt

  assign f_out[4:2] = {flags[4], Rb[0], flags[2]};
  assign result[14:0] = Rb[15:1];

  // Notes on the sheet:
  //   Similar to LSL, this shift the digits in a reverse way
endmodule

module LSR8 (
  input  [4:0] flags,
  input  [15:0] Rb,
  output [15:0] result,
  output [4:0] f_out
);

  Comparator #(.width(16)) comparator_1 (
    .a({Rb[7:0], {8{1'b0}}}), .b({16{1'b0}}), .eq(f_out[1]), .lt(f_out[0]));  // open: gt

  assign f_out[4:2] = flags[4:2];
  assign result = {Rb[7:0], {8{1'b0}}};

  // Notes on the sheet:
  //   LSL8 instruction
  //   the eight-bit shift operations shift in zeros, regardless of the carry-blog(F4) flag.
endmodule

module LU (
  input  [15:0] Ra,
  input  [15:0] Rb,
  input  [3:0] opCode,
  input  [4:0] f_in,
  output [15:0] result,
  output [4:0] f_out
);

  wire [15:0] and_1_out, or_1_out, xor_1_out;

  assign and_1_out = Ra & Rb;  // AND_Gate and_1, 16 bits wide
  assign or_1_out = Ra | Rb;  // OR_Gate or_1, 16 bits wide
  assign xor_1_out = Ra ^ Rb;  // XOR_Gate xor_1, 16 bits wide
  Multiplexer #(.select(4), .width(16)) multiplexer_1 (
    .in0({16{1'b0}}), .in1({16{1'b0}}), .in2({16{1'b0}}), .in3({16{1'b0}}), .in4({16{1'b0}}),
    .in5({16{1'b0}}), .in6({16{1'b0}}), .in7({16{1'b0}}), .in8(and_1_out), .in9(or_1_out), .in10({16{1'b0}}),
    .in11({16{1'b0}}), .in12({16{1'b0}}), .in13(xor_1_out), .in14({16{1'b0}}), .in15({16{1'b0}}),
    .out({f_out[0], result[14:0]}), .sel(opCode));
  nor nor_1 (f_out[1], result[0], result[1], result[2], result[3], result[4], result[5], result[6], result[7], result[8], result[9], result[10], result[11], result[12], result[13], result[14], f_out[0]);

  assign f_out[4:2] = f_in[4:2];
  assign result[15] = f_out[0];
endmodule

module mem_flags (
  input  [4:0] f_in,
  input  [15:0] ram_in,
  output [4:0] f_out
);

  nor nor_1 (f_out[1], ram_in[0], ram_in[1], ram_in[2], ram_in[3], ram_in[4], ram_in[5], ram_in[6], ram_in[7], ram_in[8], ram_in[9], ram_in[10], ram_in[11], ram_in[12], ram_in[13], ram_in[14], ram_in[15]);

  assign {f_out[4:2], f_out[0]} = {f_in[4:2], ram_in[15]};
endmodule

module MUL (
  input  [4:0] f_in,
  input  [15:0] Ra,
  input  [15:0] Rb,
  output [15:0] result,
  output [4:0] f_out
);

  wire comparator_1_gt, comparator_1_lt, comparator_2_gt, comparator_2_lt, nor_1_out, or_1_out, or_2_out,
       or_3_out;
  wire [15:0] bit_extender_1_out, multiplier_1_cout, multiplier_1_out, multiplier_2_cout;

  Multiplier #(.mode("twosComplement"), .width(16)) multiplier_1 (
    .a(Ra), .b(Rb), .out(multiplier_1_out), .cin({16{1'b0}}), .cout(multiplier_1_cout));
  Multiplier #(.width(16)) multiplier_2 (.a(Rb), .b(Ra), .cin({16{1'b0}}), .cout(multiplier_2_cout));  // open: out
  assign bit_extender_1_out = {{15{multiplier_1_out[15]}}, multiplier_1_out[15]};  // Bit_Extender bit_extender_1
  nor nor_1 (nor_1_out, f_in[0], f_in[1], f_in[2], f_in[3]);
  or or_1 (or_1_out, comparator_1_gt, comparator_1_lt);
  Comparator #(.width(16)) comparator_1 (
    .a(bit_extender_1_out), .b(multiplier_1_cout), .gt(comparator_1_gt), .lt(comparator_1_lt));  // open: eq
  or or_2 (or_2_out, comparator_2_gt, comparator_2_lt);
  Comparator #(.width(16)) comparator_2 (
    .a({16{1'b0}}), .b(multiplier_2_cout), .gt(comparator_2_gt), .lt(comparator_2_lt));  // open: eq
  or or_3 (or_3_out, nor_1_out, f_in[4]);
  Multiplexer #(.width(16)) multiplexer_1 (
    .in0(multiplier_1_cout), .in1(multiplier_1_out), .out(result), .sel(or_3_out));
  and and_1 (f_out[2], or_3_out, or_1_out);
  and and_2 (f_out[3], or_3_out, or_2_out);
  Comparator #(.width(16)) comparator_3 (.a({16{1'b0}}), .b(result), .gt(f_out[0]), .eq(f_out[1]));  // open: lt

  assign f_out[4] = f_in[4];

  // Notes on the sheet:
  //   low 16 if CB on or other flags all zero
  //   else high 16 of signed interpretation
  //   Overflow is signed interpretation
  //   Carry is unsigned interpretation
endmodule

module RegEnable (
  input  [3:0] opcode,
  input  [3:0] d,
  input  [3:0] a,
  input  [3:0] b,
  input  Store,
  output R1,
  output R2,
  output R3,
  output R4,
  output R5,
  output R6,
  output R7,
  output R8,
  output R9,
  output R10,
  output R11,
  output R12,
  output R13,
  output R14,
  output R15
);

  wire comparator_1_eq, comparator_2_eq, enable_ab, enable_d, is_branch, is_call, is_flaggy;
  wire [14:0] or_2_out;
  wire [15:0] decoder_1_out0, decoder_2_out0, decoder_3_out0;

  nor nor_1 (enable_d, is_branch, is_call, is_flaggy, Store);
  and and_1 (enable_ab, is_call, ~Store);  // AND_Gate
  and and_2 (is_call, ~opcode[3], ~opcode[2], opcode[1], ~opcode[0], ~d[3], ~d[2]);  // AND_Gate
  nor nor_2 (is_branch, opcode[1], opcode[2], opcode[3]);
  Comparator comparator_1 (.a({opcode, a}), .b(8'h36), .eq(comparator_1_eq));  // open: gt, lt
  or or_1 (is_flaggy, comparator_1_eq, comparator_2_eq);
  Comparator #(.width(12)) comparator_2 (.a({opcode, a, b}), .b(12'h378), .eq(comparator_2_eq));  // open: gt, lt
  Decoder #(.select(4)) decoder_1 (
    .out0(decoder_1_out0[0]), .out1(decoder_1_out0[1]), .out2(decoder_1_out0[2]), .out3(decoder_1_out0[3]),
    .out4(decoder_1_out0[4]), .out5(decoder_1_out0[5]), .out6(decoder_1_out0[6]), .out7(decoder_1_out0[7]),
    .out8(decoder_1_out0[8]), .out9(decoder_1_out0[9]), .out10(decoder_1_out0[10]),
    .out11(decoder_1_out0[11]), .out12(decoder_1_out0[12]), .out13(decoder_1_out0[13]),
    .out14(decoder_1_out0[14]), .out15(decoder_1_out0[15]), .sel(d), .en(enable_d));
  Decoder #(.select(4)) decoder_2 (
    .out0(decoder_2_out0[0]), .out1(decoder_2_out0[1]), .out2(decoder_2_out0[2]), .out3(decoder_2_out0[3]),
    .out4(decoder_2_out0[4]), .out5(decoder_2_out0[5]), .out6(decoder_2_out0[6]), .out7(decoder_2_out0[7]),
    .out8(decoder_2_out0[8]), .out9(decoder_2_out0[9]), .out10(decoder_2_out0[10]),
    .out11(decoder_2_out0[11]), .out12(decoder_2_out0[12]), .out13(decoder_2_out0[13]),
    .out14(decoder_2_out0[14]), .out15(decoder_2_out0[15]), .sel(a), .en(enable_ab));
  Decoder #(.select(4)) decoder_3 (
    .out0(decoder_3_out0[0]), .out1(decoder_3_out0[1]), .out2(decoder_3_out0[2]), .out3(decoder_3_out0[3]),
    .out4(decoder_3_out0[4]), .out5(decoder_3_out0[5]), .out6(decoder_3_out0[6]), .out7(decoder_3_out0[7]),
    .out8(decoder_3_out0[8]), .out9(decoder_3_out0[9]), .out10(decoder_3_out0[10]),
    .out11(decoder_3_out0[11]), .out12(decoder_3_out0[12]), .out13(decoder_3_out0[13]),
    .out14(decoder_3_out0[14]), .out15(decoder_3_out0[15]), .sel(b), .en(enable_ab));
  assign {R15, or_2_out[14], R13, R12, R11, R10, R9, R8, R7, R6, R5, R4, R3, R2, R1, or_2_out[0]} = decoder_1_out0 | decoder_2_out0 | decoder_3_out0;  // OR_Gate or_2, 16 bits wide
  or or_3 (R14, is_call, or_2_out[14]);

  // Other names for the same wires on the sheet: instruction[15:0] = {opcode, d, a, b}; st = Store

  // Notes on the sheet:
  //   for most instructions, enable the register indicated by d
  //   for call and return, ignore d and instead enable a/b and fp
endmodule

module RegisterBank (
  input  reset,
  input  [15:0] Rd_in,
  input  Clock,
  input  [15:0] PC_in,
  input  [15:0] Instruction,
  input  STORE,
  output [15:0] Ra_out,
  output [15:0] Rb_out,
  output [15:0] Rd_out,
  output [63:0] Rg_1,
  output [63:0] Rg_2,
  output [63:0] Rg_3,
  output [47:0] Rg_4
);

  wire enR1, enR2, enR3, enR4, enR5, enR6, enR7, enR8, enR9, enR10, enR11, enR12, enR13, enR14, enR15;
  wire [15:0] adder_1_out, R0, toR0, toR1, toR2, toR3, toR4, toR5, toR6, toR7, toR8, toR9, toR10, toR11,
       toR12, toR13, toR14, toR15;

  Adder #(.width(16)) adder_1 (.a(PC_in), .b({16{1'b0}}), .out(adder_1_out), .cin(1'b1));  // open: cout
  RegSelect regselect_1 (
    .Instruction(Instruction), .Rd(Rd_in), .New_PC(adder_1_out), .Old_FP(Rg_4[31:16]), .R1(toR1), .R2(toR2),
    .R3(toR3), .R4(toR4), .R5(toR5), .R6(toR6), .R7(toR7), .R8(toR8), .R9(toR9), .R10(toR10), .R11(toR11),
    .R12(toR12), .R13(toR13), .R14(toR14), .R15(toR15));
  RegEnable regenable_1 (
    .opcode(Instruction[15:12]), .d(Instruction[11:8]), .a(Instruction[7:4]), .b(Instruction[3:0]),
    .Store(STORE), .R1(enR1), .R2(enR2), .R3(enR3), .R4(enR4), .R5(enR5), .R6(enR6), .R7(enR7), .R8(enR8),
    .R9(enR9), .R10(enR10), .R11(enR11), .R12(enR12), .R13(enR13), .R14(enR14), .R15(enR15));
  Register #(.width(16)) u_R0 (.D(toR0), .en(1'b0), .clk(Clock), .Q(R0), .clr(reset));
  Register #(.width(16)) R1 (.D(toR1), .en(enR1), .clk(Clock), .Q(Rg_1[15:0]), .clr(reset));
  Register #(.width(16)) R2 (.D(toR2), .en(enR2), .clk(Clock), .Q(Rg_1[31:16]), .clr(reset));
  Register #(.width(16)) R3 (.D(toR3), .en(enR3), .clk(Clock), .Q(Rg_1[47:32]), .clr(reset));
  Register #(.width(16)) R4 (.D(toR4), .en(enR4), .clk(Clock), .Q(Rg_1[63:48]), .clr(reset));
  Register #(.width(16)) R5 (.D(toR5), .en(enR5), .clk(Clock), .Q(Rg_2[15:0]), .clr(reset));
  Register #(.width(16)) R6 (.D(toR6), .en(enR6), .clk(Clock), .Q(Rg_2[31:16]), .clr(reset));
  Register #(.width(16)) R7 (.D(toR7), .en(enR7), .clk(Clock), .Q(Rg_2[47:32]), .clr(reset));
  Register #(.width(16)) R8 (.D(toR8), .en(enR8), .clk(Clock), .Q(Rg_2[63:48]), .clr(reset));
  Register #(.width(16)) R9 (.D(toR9), .en(enR9), .clk(Clock), .Q(Rg_3[15:0]), .clr(reset));
  Register #(.width(16)) R10 (.D(toR10), .en(enR10), .clk(Clock), .Q(Rg_3[31:16]), .clr(reset));
  Register #(.width(16)) R11 (.D(toR11), .en(enR11), .clk(Clock), .Q(Rg_3[47:32]), .clr(reset));
  Register #(.width(16)) R12 (.D(toR12), .en(enR12), .clk(Clock), .Q(Rg_3[63:48]), .clr(reset));
  Register #(.width(16)) R13 (.D(toR13), .en(enR13), .clk(Clock), .Q(Rg_4[15:0]), .clr(reset));
  Register #(.width(16)) R14 (.D(Ra_out), .en(enR14), .clk(Clock), .Q(Rg_4[31:16]), .clr(reset));
  Register #(.width(16)) R15 (.D(toR15), .en(enR15), .clk(Clock), .Q(Rg_4[47:32]), .clr(reset));
  Multiplexer #(.select(4), .width(16)) multiplexer_1 (
    .in0(R0), .in1(Rg_1[15:0]), .in2(Rg_1[31:16]), .in3(Rg_1[47:32]), .in4(Rg_1[63:48]), .in5(Rg_2[15:0]),
    .in6(Rg_2[31:16]), .in7(Rg_2[47:32]), .in8(Rg_2[63:48]), .in9(Rg_3[15:0]), .in10(Rg_3[31:16]),
    .in11(Rg_3[47:32]), .in12(Rg_3[63:48]), .in13(Rg_4[15:0]), .in14(Rg_4[31:16]), .in15(Rg_4[47:32]),
    .out(Ra_out), .sel(Instruction[7:4]));
  Multiplexer #(.select(4), .width(16)) multiplexer_2 (
    .in0(R0), .in1(Rg_1[15:0]), .in2(Rg_1[31:16]), .in3(Rg_1[47:32]), .in4(Rg_1[63:48]), .in5(Rg_2[15:0]),
    .in6(Rg_2[31:16]), .in7(Rg_2[47:32]), .in8(Rg_2[63:48]), .in9(Rg_3[15:0]), .in10(Rg_3[31:16]),
    .in11(Rg_3[47:32]), .in12(Rg_3[63:48]), .in13(Rg_4[15:0]), .in14(Rg_4[31:16]), .in15(Rg_4[47:32]),
    .out(Rb_out), .sel(Instruction[3:0]));
  Multiplexer #(.select(4), .width(16)) multiplexer_3 (
    .in0(R0), .in1(Rg_1[15:0]), .in2(Rg_1[31:16]), .in3(Rg_1[47:32]), .in4(Rg_1[63:48]), .in5(Rg_2[15:0]),
    .in6(Rg_2[31:16]), .in7(Rg_2[47:32]), .in8(Rg_2[63:48]), .in9(Rg_3[15:0]), .in10(Rg_3[31:16]),
    .in11(Rg_3[47:32]), .in12(Rg_3[63:48]), .in13(Rg_4[15:0]), .in14(Rg_4[31:16]), .in15(Rg_4[47:32]),
    .out(Rd_out), .sel(Instruction[11:8]));

  // Other names for the same wires on the sheet: Clk = Clock; FP[15:0] = Ra_out; b[3:0] = Instruction[3:0];
  //   a[3:0] = Instruction[7:4]; d[3:0] = Instruction[11:8]; op[3:0] = Instruction[15:12]; r = reset;
  //   Rd[15:0] = Rd_in; R1[15:0] = Rg_1[15:0]; R2[15:0] = Rg_1[31:16]; R3[15:0] = Rg_1[47:32]; R4[15:0] = Rg_1[63:48];
  //   R5[15:0] = Rg_2[15:0]; R6[15:0] = Rg_2[31:16]; R7[15:0] = Rg_2[47:32]; R8[15:0] = Rg_2[63:48];
  //   R9[15:0] = Rg_3[15:0]; R10[15:0] = Rg_3[31:16]; R11[15:0] = Rg_3[47:32]; R12[15:0] = Rg_3[63:48];
  //   R13[15:0] = Rg_4[15:0]; R14[15:0] = Rg_4[31:16]; R15[15:0] = Rg_4[47:32]; st = STORE

  // Notes on the sheet:
  //   On a CALL/RETURN:
  //   PC+1 into Rb
  //   Old FP into Ra
  //   Determine which register(s) to write
  //   If storing to RAM: none
  //   Determine which data to write
  //   R0 fixed at 0
  //   R11-R13 have special usage
  //   (function calls, branching, etc.)
  //   R14 = FP (frame pointer)
  //   R15 = SP (stack pointer)
  //   selecting which registers to push out
  //   for main circuit displaying purposes
  //   Ra goes into FP
endmodule

module RegSelect (
  input  [15:0] Instruction,
  input  [15:0] Rd,
  input  [15:0] New_PC,
  input  [15:0] Old_FP,
  output [15:0] R1,
  output [15:0] R2,
  output [15:0] R3,
  output [15:0] R4,
  output [15:0] R5,
  output [15:0] R6,
  output [15:0] R7,
  output [15:0] R8,
  output [15:0] R9,
  output [15:0] R10,
  output [15:0] R11,
  output [15:0] R12,
  output [15:0] R13,
  output [15:0] R14,
  output [15:0] R15
);

  wire and_1_out;
  wire [15:0] demultiplexer_1_out1, demultiplexer_1_out2, demultiplexer_1_out3, demultiplexer_1_out4,
       demultiplexer_1_out5, demultiplexer_1_out6, demultiplexer_1_out7, demultiplexer_1_out8,
       demultiplexer_1_out9, demultiplexer_1_out10, demultiplexer_1_out11, demultiplexer_1_out12,
       demultiplexer_1_out13, demultiplexer_1_out14, demultiplexer_1_out15, demultiplexer_2_out1,
       demultiplexer_2_out2, demultiplexer_2_out3, demultiplexer_2_out4, demultiplexer_2_out5,
       demultiplexer_2_out6, demultiplexer_2_out7, demultiplexer_2_out8, demultiplexer_2_out9,
       demultiplexer_2_out10, demultiplexer_2_out11, demultiplexer_2_out12, demultiplexer_2_out13,
       demultiplexer_2_out14, demultiplexer_2_out15, or_1_out, or_2_out, or_3_out, or_4_out, or_5_out,
       or_6_out, or_7_out, or_8_out, or_9_out, or_10_out, or_11_out, or_12_out, or_13_out, or_14_out,
       or_15_out;

  Demultiplexer #(.select(4), .width(16)) demultiplexer_1 (
    .out1(demultiplexer_1_out1), .out2(demultiplexer_1_out2), .out3(demultiplexer_1_out3),
    .out4(demultiplexer_1_out4), .out5(demultiplexer_1_out5), .out6(demultiplexer_1_out6),
    .out7(demultiplexer_1_out7), .out8(demultiplexer_1_out8), .out9(demultiplexer_1_out9),
    .out10(demultiplexer_1_out10), .out11(demultiplexer_1_out11), .out12(demultiplexer_1_out12),
    .out13(demultiplexer_1_out13), .out14(demultiplexer_1_out14), .out15(demultiplexer_1_out15), .in(Old_FP),
    .sel(Instruction[7:4]));  // open: out0
  Demultiplexer #(.select(4), .width(16)) demultiplexer_2 (
    .out1(demultiplexer_2_out1), .out2(demultiplexer_2_out2), .out3(demultiplexer_2_out3),
    .out4(demultiplexer_2_out4), .out5(demultiplexer_2_out5), .out6(demultiplexer_2_out6),
    .out7(demultiplexer_2_out7), .out8(demultiplexer_2_out8), .out9(demultiplexer_2_out9),
    .out10(demultiplexer_2_out10), .out11(demultiplexer_2_out11), .out12(demultiplexer_2_out12),
    .out13(demultiplexer_2_out13), .out14(demultiplexer_2_out14), .out15(demultiplexer_2_out15), .in(New_PC),
    .sel(Instruction[3:0]));  // open: out0
  and and_1 (and_1_out, ~Instruction[15], ~Instruction[14], Instruction[13], ~Instruction[12], ~Instruction[11], ~Instruction[10]);  // AND_Gate
  assign or_1_out = demultiplexer_2_out1 | demultiplexer_1_out1;  // OR_Gate or_1, 16 bits wide
  assign or_2_out = demultiplexer_2_out2 | demultiplexer_1_out2;  // OR_Gate or_2, 16 bits wide
  assign or_3_out = demultiplexer_2_out3 | demultiplexer_1_out3;  // OR_Gate or_3, 16 bits wide
  assign or_4_out = demultiplexer_2_out4 | demultiplexer_1_out4;  // OR_Gate or_4, 16 bits wide
  assign or_5_out = demultiplexer_2_out5 | demultiplexer_1_out5;  // OR_Gate or_5, 16 bits wide
  assign or_6_out = demultiplexer_2_out6 | demultiplexer_1_out6;  // OR_Gate or_6, 16 bits wide
  assign or_7_out = demultiplexer_2_out7 | demultiplexer_1_out7;  // OR_Gate or_7, 16 bits wide
  assign or_8_out = demultiplexer_2_out8 | demultiplexer_1_out8;  // OR_Gate or_8, 16 bits wide
  assign or_9_out = demultiplexer_2_out9 | demultiplexer_1_out9;  // OR_Gate or_9, 16 bits wide
  assign or_10_out = demultiplexer_2_out10 | demultiplexer_1_out10;  // OR_Gate or_10, 16 bits wide
  assign or_11_out = demultiplexer_2_out11 | demultiplexer_1_out11;  // OR_Gate or_11, 16 bits wide
  assign or_12_out = demultiplexer_2_out12 | demultiplexer_1_out12;  // OR_Gate or_12, 16 bits wide
  assign or_13_out = demultiplexer_2_out13 | demultiplexer_1_out13;  // OR_Gate or_13, 16 bits wide
  assign or_14_out = demultiplexer_2_out14 | demultiplexer_1_out14;  // OR_Gate or_14, 16 bits wide
  assign or_15_out = demultiplexer_2_out15 | demultiplexer_1_out15;  // OR_Gate or_15, 16 bits wide
  Multiplexer #(.width(16)) multiplexer_1 (.in0(Rd), .in1(or_1_out), .out(R1), .sel(and_1_out));
  Multiplexer #(.width(16)) multiplexer_2 (.in0(Rd), .in1(or_2_out), .out(R2), .sel(and_1_out));
  Multiplexer #(.width(16)) multiplexer_3 (.in0(Rd), .in1(or_3_out), .out(R3), .sel(and_1_out));
  Multiplexer #(.width(16)) multiplexer_4 (.in0(Rd), .in1(or_4_out), .out(R4), .sel(and_1_out));
  Multiplexer #(.width(16)) multiplexer_5 (.in0(Rd), .in1(or_5_out), .out(R5), .sel(and_1_out));
  Multiplexer #(.width(16)) multiplexer_6 (.in0(Rd), .in1(or_6_out), .out(R6), .sel(and_1_out));
  Multiplexer #(.width(16)) multiplexer_7 (.in0(Rd), .in1(or_7_out), .out(R7), .sel(and_1_out));
  Multiplexer #(.width(16)) multiplexer_8 (.in0(Rd), .in1(or_8_out), .out(R8), .sel(and_1_out));
  Multiplexer #(.width(16)) multiplexer_9 (.in0(Rd), .in1(or_9_out), .out(R9), .sel(and_1_out));
  Multiplexer #(.width(16)) multiplexer_10 (.in0(Rd), .in1(or_10_out), .out(R10), .sel(and_1_out));
  Multiplexer #(.width(16)) multiplexer_11 (.in0(Rd), .in1(or_11_out), .out(R11), .sel(and_1_out));
  Multiplexer #(.width(16)) multiplexer_12 (.in0(Rd), .in1(or_12_out), .out(R12), .sel(and_1_out));
  Multiplexer #(.width(16)) multiplexer_13 (.in0(Rd), .in1(or_13_out), .out(R13), .sel(and_1_out));
  Multiplexer #(.width(16)) multiplexer_14 (.in0(Rd), .in1(or_14_out), .out(R14), .sel(and_1_out));
  Multiplexer #(.width(16)) multiplexer_15 (.in0(Rd), .in1(or_15_out), .out(R15), .sel(and_1_out));

  // Notes on the sheet:
  //   If CALL/RETURN, FP into A and PC into B
endmodule

module sethi (
  input  [15:0] Rb,
  input  [3:0] b0_3,
  input  [3:0] b4_7,
  output [15:0] result
);

  Bit_Extender #(.in_width(16), .out_width(8)) bit_extender_1 (.in(Rb), .out(result[7:0]));

  assign result[15:8] = {b4_7, b0_3};
endmodule

module setlo (
  input  [3:0] b0_3,
  input  [3:0] b4_7,
  output [15:0] result
);

  assign result = {{8{b4_7[3]}}, {b4_7, b0_3}};  // Bit_Extender bit_extender_1
endmodule

module shifts (
  input  [4:0] flags_in,
  input  [15:0] Rb,
  input  [15:0] Rd,
  input  [3:0] b0_3,
  input  [3:0] b4_7,
  input  [3:0] b8_11,
  output [15:0] result,
  output [4:0] f_out
);

  wire [4:0] asl_1_f_out, asr_1_f_out, flags_1_flags_out, inc_dec_1_flags_out, lsl8_1_f_out, lsl_1_f_out,
       lsr8_1_f_out, lsr_1_f_out, multiplexer_2_out;
  wire [15:0] asl_1_result, asr_1_result, flags_1_result, inc_dec_1_result, lsl8_1_result, lsl_1_result,
       lsr8_1_result, lsr_1_result, multiplexer_1_out;

  LSL lsl_1 (.flags(flags_in), .Rb(Rb), .result(lsl_1_result), .f_out(lsl_1_f_out));
  LSR lsr_1 (.flags(flags_in), .Rb(Rb), .result(lsr_1_result), .f_out(lsr_1_f_out));
  LSL8 lsl8_1 (.flags(flags_in), .Rb(Rb), .result(lsl8_1_result), .f_out(lsl8_1_f_out));
  LSR8 lsr8_1 (.flags(flags_in), .Rb(Rb), .result(lsr8_1_result), .f_out(lsr8_1_f_out));
  ASL asl_1 (.flags(flags_in), .Rb(Rb), .result(asl_1_result), .f_out(asl_1_f_out));
  ASR asr_1 (.flags(flags_in), .Rb(Rb), .result(asr_1_result), .f_out(asr_1_f_out));
  flags flags_1 (
    .flags_in(flags_in), .Rd(Rd), .b0_3(b0_3), .b4_7(b4_7), .b8_11(b8_11), .result(flags_1_result),
    .flags_out(flags_1_flags_out));
  INC_DEC inc_dec_1 (
    .flags_in(flags_in), .Rd(Rd), .b0_3(b0_3), .b4_7(b4_7), .result(inc_dec_1_result),
    .flags_out(inc_dec_1_flags_out));
  Multiplexer #(.select(3), .width(16)) multiplexer_1 (
    .in0(lsl_1_result), .in1(lsr_1_result), .in2(lsl8_1_result), .in3(lsr8_1_result), .in4(asl_1_result),
    .in5(asr_1_result), .in6(flags_1_result), .in7(flags_1_result), .out(multiplexer_1_out), .sel(b4_7[2:0]));
  Multiplexer #(.select(3), .width(5)) multiplexer_2 (
    .in0(lsl_1_f_out), .in1(lsr_1_f_out), .in2(lsl8_1_f_out), .in3(lsr8_1_f_out), .in4(asl_1_f_out),
    .in5(asr_1_f_out), .in6(flags_1_flags_out), .in7(flags_1_flags_out), .out(multiplexer_2_out),
    .sel(b4_7[2:0]));
  Multiplexer #(.width(16)) multiplexer_3 (
    .in0(multiplexer_1_out), .in1(inc_dec_1_result), .out(result), .sel(b4_7[3]));
  Multiplexer #(.width(5)) multiplexer_4 (
    .in0(multiplexer_2_out), .in1(inc_dec_1_flags_out), .out(f_out), .sel(b4_7[3]));

  // Notes on the sheet:
  //   all the "3" instructions, shifts, direct flag changes and INC/DEC
endmodule
